// Digital circuit Bin2Hex.dig as structural Verilog
module Bin2Hex (
  input  A0,
  input  A1,
  input  A2,
  input  A3,
  output [3:0] d,
  output dp
);

  LookUpTable #(.Bits(4)) Binary_to_Hex (.in0(A0), .in1(A1), .in2(A2), .in3(A3), .out(d));
  // Pins of 1 and 4 bits meet at d

  assign dp = 1'b0;

  // Notes on the sheet:
  //   contents of Binary_to_Hex (hex, n*v repeats v):
  //   0,1,2,3,4,5,6,7,8,9,a,b,c,d,e,f
endmodule
