// Digital circuit ChasingUpDownCounters.dig as structural Verilog
module ChasingUpDownCounters (
  input  clk,
  input  nPL
);

  wire _7483_1_p12, _7483_1_p13, _7483_1_p14, _7483_1_p15, _74191_1_p3, _74191_1_p11, _74191_1_p12,
       _74191_1_p13, _74191_1_p14, _74191_2_p3, _74191_2_p11, _74191_2_p12, _74191_2_p13, _74191_2_p14,
       bin2hex_1_p6, bin2hex_2_p6, bin2hex_3_p6, bin2hex_4_p6, bin2hex_5_p6, bin2hex_6_p6, bin2hex_7_p6,
       bin2hex_8_p6, bin2hex_9_p6, clockdivider_1_c, clockdivider_1_hc, d_ff_1_q, d_ff_2_q, d_ff_3_q,
       d_ff_4_q, d_ff_5_q, d_ff_6_q, d_ff_7_q, d_ff_8_q, d_ff_9_q, d_ff_10_q, d_ff_11_q, d_ff_12_q,
       d_ff_13_q, d_ff_14_q, d_ff_15_q, d_ff_16_q, d_ff_17_q, d_ff_18_q, d_ff_19_q, d_ff_20_q, d_ff_21_q,
       d_ff_22_q, d_ff_23_q, d_ff_24_q, nor_1_out, nor_2_out, not_1_out, not_2_out, not_3_out, not_4_out,
       not_5_out, not_6_out, not_7_out, switch_1_b, switch_2_b, switch_3_b, xor_1_out;
  wire [3:0] bin2hex_1_p5, bin2hex_2_p5, bin2hex_3_p5, bin2hex_4_p5, bin2hex_5_p5, bin2hex_6_p5,
       bin2hex_7_p5, bin2hex_8_p5, bin2hex_9_p5;

  Switch switch_1 (.A(1'b1), .B(switch_1_b));
  Switch switch_2 (.A(1'b1), .B(switch_2_b));
  Switch switch_3 (.A(1'b1), .B(switch_3_b));
  PullDown pulldown_1 (.out(switch_3_b));
  PullDown pulldown_2 (.out(switch_2_b));
  PullDown pulldown_3 (.out(switch_1_b));
  // Bin2Hex bin2hex_1: pin names not known; wires that end beside it: switch_2_b, switch_3_b, 1'b0, 1'b0, bin2hex_1_p5, bin2hex_1_p6, switch_1_b, switch_2_b, switch_3_b
  Seven_Seg_Hex seven_seg_hex_1 (.d(bin2hex_1_p5), .dp(bin2hex_1_p6));
  ClockDivider clockdivider_1 (.IN(clk), .C(clockdivider_1_c), .HC(clockdivider_1_hc));
  // _74191 _74191_1: pin names not known; wires that end beside it: 1'b0, nPL, _74191_1_p3, clockdivider_1_c, 1'b0, 1'b0, 1'b0, 1'b0, 1'b1, 1'b0, _74191_1_p11, _74191_1_p12, _74191_1_p13, _74191_1_p14
  // _74191 _74191_2: pin names not known; wires that end beside it: 1'b0, nPL, _74191_2_p3, clockdivider_1_c, 1'b0, 1'b0, 1'b0, 1'b1, 1'b1, 1'b0, _74191_2_p11, _74191_2_p12, _74191_2_p13, _74191_2_p14
  nor nor_1 (nor_1_out, _74191_1_p11, _74191_1_p12, _74191_1_p13, _74191_1_p14);
  nor nor_2 (nor_2_out, _74191_2_p11, _74191_2_p12, _74191_2_p13, _74191_2_p14);
  Seven_Seg_Hex seven_seg_hex_2 (.d(bin2hex_2_p5), .dp(bin2hex_2_p6));
  // Bin2Hex bin2hex_2: pin names not known; wires that end beside it: _74191_1_p11, _74191_1_p12, _74191_1_p13, _74191_1_p14, bin2hex_2_p5, bin2hex_2_p6
  RS_FF_AS rs_ff_as_1 (.S(_74191_1_p14), .R(nor_1_out), .Q(_74191_1_p3));  // open: nQ
  Seven_Seg_Hex seven_seg_hex_3 (.d(bin2hex_3_p5), .dp(bin2hex_3_p6));
  // Bin2Hex bin2hex_3: pin names not known; wires that end beside it: _74191_2_p11, _74191_2_p12, _74191_2_p13, _74191_2_p14, bin2hex_3_p5, bin2hex_3_p6
  RS_FF_AS rs_ff_as_2 (.S(_74191_2_p14), .R(nor_2_out), .Q(_74191_2_p3));  // open: nQ
  xor xor_1 (xor_1_out, clockdivider_1_hc, _74191_1_p11);
  not not_1 (not_1_out, _74191_1_p11);
  not not_2 (not_2_out, _74191_1_p11);
  not not_3 (not_3_out, _74191_1_p12);
  not not_4 (not_4_out, _74191_1_p13);
  not not_5 (not_5_out, _74191_1_p14);
  not not_6 (not_6_out, _74191_2_p11);
  // _7483 _7483_1: pin names not known; wires that end beside it: 1'b1, not_2_out, not_3_out, not_4_out, not_5_out, 1'b0, 1'b0, 1'b0, 1'b1, 1'b1, 1'b0, _7483_1_p12, _7483_1_p13, _7483_1_p14, _7483_1_p15
  LED led_1 (.in(xor_1_out));
  D_FF d_ff_1 (.D(_74191_1_p11), .C(_74191_1_p11), .Q(d_ff_1_q));  // open: nQ
  D_FF d_ff_2 (.D(_74191_1_p12), .C(_74191_1_p11), .Q(d_ff_2_q));  // open: nQ
  D_FF d_ff_3 (.D(_74191_1_p13), .C(_74191_1_p11), .Q(d_ff_3_q));  // open: nQ
  D_FF d_ff_4 (.D(_74191_1_p14), .C(_74191_1_p11), .Q(d_ff_4_q));  // open: nQ
  D_FF d_ff_5 (.D(_74191_1_p11), .C(not_1_out), .Q(d_ff_5_q));  // open: nQ
  D_FF d_ff_6 (.D(_74191_1_p12), .C(not_1_out), .Q(d_ff_6_q));  // open: nQ
  D_FF d_ff_7 (.D(_74191_1_p13), .C(not_1_out), .Q(d_ff_7_q));  // open: nQ
  D_FF d_ff_8 (.D(_74191_1_p14), .C(not_1_out), .Q(d_ff_8_q));  // open: nQ
  D_FF d_ff_9 (.D(_74191_2_p11), .C(_74191_2_p11), .Q(d_ff_9_q));  // open: nQ
  D_FF d_ff_10 (.D(_74191_2_p12), .C(_74191_2_p11), .Q(d_ff_10_q));  // open: nQ
  D_FF d_ff_11 (.D(_74191_2_p13), .C(_74191_2_p11), .Q(d_ff_11_q));  // open: nQ
  D_FF d_ff_12 (.D(_74191_2_p14), .C(_74191_2_p11), .Q(d_ff_12_q));  // open: nQ
  D_FF d_ff_13 (.D(_74191_2_p11), .C(not_6_out), .Q(d_ff_13_q));  // open: nQ
  D_FF d_ff_14 (.D(_74191_2_p12), .C(not_6_out), .Q(d_ff_14_q));  // open: nQ
  D_FF d_ff_15 (.D(_74191_2_p13), .C(not_6_out), .Q(d_ff_15_q));  // open: nQ
  D_FF d_ff_16 (.D(_74191_2_p14), .C(not_6_out), .Q(d_ff_16_q));  // open: nQ
  // Bin2Hex bin2hex_4: pin names not known; wires that end beside it: d_ff_1_q, d_ff_2_q, d_ff_3_q, d_ff_4_q, bin2hex_4_p5, bin2hex_4_p6
  // Bin2Hex bin2hex_5: pin names not known; wires that end beside it: d_ff_5_q, d_ff_6_q, d_ff_7_q, d_ff_8_q, bin2hex_5_p5, bin2hex_5_p6
  // Bin2Hex bin2hex_6: pin names not known; wires that end beside it: d_ff_9_q, d_ff_10_q, d_ff_11_q, d_ff_12_q, bin2hex_6_p5, bin2hex_6_p6
  // Bin2Hex bin2hex_7: pin names not known; wires that end beside it: d_ff_13_q, d_ff_14_q, d_ff_15_q, d_ff_16_q, bin2hex_7_p5, bin2hex_7_p6
  Seven_Seg_Hex seven_seg_hex_4 (.d(bin2hex_4_p5), .dp(bin2hex_4_p6));
  Seven_Seg_Hex seven_seg_hex_5 (.d(bin2hex_5_p5), .dp(bin2hex_5_p6));
  Seven_Seg_Hex seven_seg_hex_6 (.d(bin2hex_6_p5), .dp(bin2hex_6_p6));
  Seven_Seg_Hex seven_seg_hex_7 (.d(bin2hex_7_p5), .dp(bin2hex_7_p6));
  not not_7 (not_7_out, _7483_1_p12);
  D_FF d_ff_17 (.D(_7483_1_p12), .C(_7483_1_p12), .Q(d_ff_17_q));  // open: nQ
  D_FF d_ff_18 (.D(_7483_1_p13), .C(_7483_1_p12), .Q(d_ff_18_q));  // open: nQ
  D_FF d_ff_19 (.D(_7483_1_p14), .C(_7483_1_p12), .Q(d_ff_19_q));  // open: nQ
  D_FF d_ff_20 (.D(_7483_1_p15), .C(_7483_1_p12), .Q(d_ff_20_q));  // open: nQ
  D_FF d_ff_21 (.D(_7483_1_p12), .C(not_7_out), .Q(d_ff_21_q));  // open: nQ
  D_FF d_ff_22 (.D(_7483_1_p13), .C(not_7_out), .Q(d_ff_22_q));  // open: nQ
  D_FF d_ff_23 (.D(_7483_1_p14), .C(not_7_out), .Q(d_ff_23_q));  // open: nQ
  D_FF d_ff_24 (.D(_7483_1_p15), .C(not_7_out), .Q(d_ff_24_q));  // open: nQ
  Seven_Seg_Hex seven_seg_hex_8 (.d(bin2hex_8_p5), .dp(bin2hex_8_p6));
  // Bin2Hex bin2hex_8: pin names not known; wires that end beside it: d_ff_17_q, d_ff_18_q, d_ff_19_q, d_ff_20_q, bin2hex_8_p5, bin2hex_8_p6
  Seven_Seg_Hex seven_seg_hex_9 (.d(bin2hex_9_p5), .dp(bin2hex_9_p6));
  // Bin2Hex bin2hex_9: pin names not known; wires that end beside it: d_ff_21_q, d_ff_22_q, d_ff_23_q, d_ff_24_q, bin2hex_9_p5, bin2hex_9_p6

  // Notes on the sheet:
  //   nPL: Preset Load (active high)
endmodule
