// Digital circuit ClockDivider.dig as structural Verilog
module ClockDivider (
  input  IN,
  output C,
  output HC
);

  // _74191 _74191_1: pin names not known; wires that end beside it: 1'b0, 1'b1, 1'b0, IN, 1'b0, 1'b0, 1'b0, 1'b0, 1'b1, 1'b0, HC

  assign C = IN;

  // Notes on the sheet:
  //   IN: Clock to be divided
  //   C: Clock pass-through
  //   HC: Half Clock
endmodule
